// Logisim project PC.circ as structural Verilog: 1 circuit, main circuit VonNeumannPC_x16
module VonNeumannPC_x16 (
);

  wire ALU_or_Data, clk, dmux8_1_out_3, dmux8_1_out_4, dmux8_1_out_5, dmux8_1_out_6, dmux8_1_out_7,
       dmux8_1_out_8, dmux8_1_out_9, dmux8_1_out_10, dmux_x_1_c0, dmux_x_1_c1, EQ, GE, GT, LE, LT,
       mux8_1_out_10, mux_x_1_out_4, mux_x_2_out_4, mux_x_3_out_4, NE, output2A;
  wire [1:0] rom_1_data_3;
  wire [2:0] rom_1_data;
  wire [14:0] alu_16_1_out_7;
  wire [14:3] rom_1_data_2;
  wire [15:0] alu_out, IO0, IO1, IO2, IO3, IO4, IO5, IO6, IO7, mem_out, mux_x16_1_out_4, pc_x16_1_out_4,
       ram_1_dout, ReadControl_out_10, reg_x16_1_out_4, regA;

  Clock clock_1 (.out(clk));
  // Probe on {ALU_or_Data, rom_1_data_2[14:10], rom_1_data_3, rom_1_data_2[7:3], rom_1_data}
  // Probe on nothing
  mux8 mux8_1 (
    .in_9(rom_1_data), .in_1(1'b1), .in_2(LE), .in_3(NE), .in_4(LT), .in_5(GE), .in_6(EQ), .in_7(GT),
    .out_10(mux8_1_out_10));  // open: in_8
  mux_x16 mux_x16_1 (.in_1(rom_1_data_2[12]), .in_2(mem_out), .in_3(regA), .out_4(mux_x16_1_out_4));
  alu_16 alu_16_1 (
    .Op_code(rom_1_data_3), .in_2(rom_1_data_2[7]), .in_3(rom_1_data_2[6]), .y(reg_x16_1_out_4),
    .in_6(mux_x16_1_out_4), .u(rom_1_data_2[10]), .out_7({LT, alu_16_1_out_7}));
  or16_x or16_x_1 (.in_1({LT, alu_16_1_out_7}), .out_2(NE));
  not_x not_x_1 (.in_1(LT), .out_2(GE));
  not_x not_x_2 (.in_1(NE), .out_2(EQ));
  // Probe on {ALU_or_Data, rom_1_data_2[14:10], rom_1_data_3, rom_1_data_2[7:3], rom_1_data}
  or_x or_x_1 (.in_1(EQ), .in_2(LT), .out_3(LE));
  ROM #(.addrWidth(16), .dataWidth(16)) rom_1 (
    .addr(pc_x16_1_out_4),
    .data({ALU_or_Data, rom_1_data_2[14:10], rom_1_data_3, rom_1_data_2[7:3], rom_1_data}));
  // Probe on mux_x_1_out_4
  mux_x mux_x_1 (.Select(ALU_or_Data), .D1(mux8_1_out_10), .D0(1'b0), .out_4(mux_x_1_out_4));
  mux_x16 mux_x16_2 (
    .in_1(ALU_or_Data), .in_2({LT, alu_16_1_out_7}),
    .in_3({ALU_or_Data, rom_1_data_2[14:10], rom_1_data_3, rom_1_data_2[7:3], rom_1_data}), .out_4(alu_out));
  mux_x mux_x_2 (.Select(ALU_or_Data), .D1(rom_1_data_2[5]), .D0(1'b1), .out_4(mux_x_2_out_4));
  mux_x mux_x_3 (.Select(ALU_or_Data), .D1(rom_1_data_2[4]), .D0(1'b0), .out_4(mux_x_3_out_4));
  mux_x mux_x_4 (.Select(ALU_or_Data), .D1(rom_1_data_2[3]), .D0(1'b0), .out_4(output2A));
  not_x not_x_3 (.in_1(LE), .out_2(GT));
  // Probe on alu_out
  // Probe on mux_x_2_out_4
  // Probe on mux_x_3_out_4
  // Probe on output2A
  // Probe on pc_x16_1_out_4
  reg_x16 reg_x16_1 (.in_1(clk), .load(mux_x_3_out_4), .data(alu_out), .out_4(reg_x16_1_out_4));
  reg_x16 reg_x16_2 (.in_1(clk), .load(mux_x_2_out_4), .data(alu_out), .out_4(regA));
  pc_x16 pc_x16_1 (.load(mux_x_1_out_4), .in_3(regA), .in_1(clk), .out_4(pc_x16_1_out_4));
  // Probe on reg_x16_1_out_4
  // Probe on regA
  dmux8 dmux8_1 (
    .in_2(dmux_x_1_c1), .in_1(regA[2:0]), .out_4(dmux8_1_out_4), .out_5(dmux8_1_out_5),
    .out_6(dmux8_1_out_6), .out_7(dmux8_1_out_7), .out_8(dmux8_1_out_8), .out_9(dmux8_1_out_9),
    .out_10(dmux8_1_out_10), .out_3(dmux8_1_out_3));
  dmux_x dmux_x_1 (.select(regA[14]), .in_2(output2A), .C1(dmux_x_1_c1), .C0(dmux_x_1_c0));
  // Probe on regA[13:0]
  RAM #(.addrWidth(14), .asyncread("true"), .dataWidth(16), .trigger("falling")) ram_1 (
    .addr(regA[13:0]), .we(dmux_x_1_c0), .oe(1'b1), .clk(clk), .din(alu_out), .dout(ram_1_dout));
  reg_x16 reg_x16_3 (.in_1(clk), .load(dmux8_1_out_3), .data(alu_out), .out_4(IO7));
  reg_x16 reg_x16_4 (.in_1(clk), .load(dmux8_1_out_4), .data(alu_out), .out_4(IO6));
  reg_x16 reg_x16_5 (.in_1(clk), .load(dmux8_1_out_5), .data(alu_out), .out_4(IO5));
  reg_x16 reg_x16_6 (.in_1(clk), .load(dmux8_1_out_6), .data(alu_out), .out_4(IO4));
  reg_x16 reg_x16_7 (.in_1(clk), .load(dmux8_1_out_7), .data(alu_out), .out_4(IO3));
  reg_x16 reg_x16_8 (.in_1(clk), .load(dmux8_1_out_8), .data(alu_out), .out_4(IO2));
  reg_x16 reg_x16_9 (.in_1(clk), .load(dmux8_1_out_9), .data(alu_out), .out_4(IO1));
  reg_x16 reg_x16_10 (.in_1(clk), .load(dmux8_1_out_10), .data(alu_out), .out_4(IO0));
  // Probe on IO7
  // Probe on IO6
  // Probe on IO5
  // Probe on IO4
  // Probe on IO3
  // Probe on IO2
  // Probe on IO1
  // Probe on IO0
  mux8_x16 ReadControl (
    .in_9(regA[2:0]), .in_1(IO7), .in_2(IO6), .in_3(IO5), .in_4(IO4), .in_5(IO3), .in_6(IO2), .in_7(IO1),
    .in_8(IO0), .out_10(ReadControl_out_10));
  mux_x16 mux_x16_3 (.in_1(regA[14]), .in_2(ReadControl_out_10), .in_3(ram_1_dout), .out_4(mem_out));
  // Probe on ReadControl_out_10
  // Probe on ram_1_dout
  // RGB_Video #(.width(256)) rgb_video_1: pin names not known; wires that end beside it: IO0[0], clk, IO6[0], IO1[7:0], IO2[6:0], {IO3[7:0], IO4[7:0], IO5[7:0]}

  // Notes on the sheet:
  //   Instruction
  //   Reg D
  //   A*
  //   Reg A
  //   (ALU) Jump Flag
  //   (ALU) Result
  //   (ALU) output to A flag
  //   ( ALU) output to D flag
  //   (ALU) output to A*
  //   memory data at address
  //   address
  //   Reg A
  //   D
  //   A
  //   0x0007
  //   0x0006
  //   0x0005
  //   0x0004
  //   0x0003
  //   0x0002
  //   0x0001
  //   0x0000
  //   X
  //   Y
  //   R
  //   G
  //   B
endmodule
