// Logisim project basic.circ as structural Verilog
module nand_x (
  input  in_1,
  input  in_2,
  output out_3
);

  nand nand_1 (out_3, in_1, in_2);
endmodule

module not_x (
  input  in_1,
  output out_2
);

  nand nand_1 (out_2, in_1, in_1);
endmodule

module and_x (
  input  in_1,
  input  in_2,
  output out_3
);

  wire nand_1_out;

  nand nand_1 (nand_1_out, in_1, in_2);
  not_x not_x_1 (.in_1(nand_1_out), .out_2(out_3));
endmodule

module or_x (
  input  in_1,
  input  in_2,
  output out_3
);

  wire not_x_1_out_2, not_x_2_out_2;

  not_x not_x_1 (.in_1(in_1), .out_2(not_x_1_out_2));
  not_x not_x_2 (.in_1(in_2), .out_2(not_x_2_out_2));
  nand nand_1 (out_3, not_x_1_out_2, not_x_2_out_2);
endmodule

module or16_x (
  input  [15:0] in_1,
  output out_2
);

  wire or_x_1_out_3, or_x_2_out_3, or_x_3_out_3, or_x_4_out_3, or_x_5_out_3, or_x_6_out_3, or_x_7_out_3,
       or_x_8_out_3, or_x_9_out_3, or_x_10_out_3, or_x_11_out_3, or_x_13_out_3, or_x_14_out_3, or_x_15_out_3;

  or_x or_x_1 (.in_1(in_1[0]), .in_2(in_1[1]), .out_3(or_x_1_out_3));
  or_x or_x_2 (.in_1(or_x_1_out_3), .in_2(in_1[2]), .out_3(or_x_2_out_3));
  or_x or_x_3 (.in_1(or_x_15_out_3), .in_2(in_1[10]), .out_3(or_x_3_out_3));
  or_x or_x_4 (.in_1(or_x_3_out_3), .in_2(in_1[11]), .out_3(or_x_4_out_3));
  or_x or_x_5 (.in_1(or_x_2_out_3), .in_2(in_1[3]), .out_3(or_x_5_out_3));
  or_x or_x_6 (.in_1(or_x_5_out_3), .in_2(in_1[4]), .out_3(or_x_6_out_3));
  or_x or_x_7 (.in_1(or_x_4_out_3), .in_2(in_1[12]), .out_3(or_x_7_out_3));
  or_x or_x_8 (.in_1(or_x_6_out_3), .in_2(in_1[5]), .out_3(or_x_8_out_3));
  or_x or_x_9 (.in_1(or_x_7_out_3), .in_2(in_1[13]), .out_3(or_x_9_out_3));
  or_x or_x_10 (.in_1(or_x_8_out_3), .in_2(in_1[6]), .out_3(or_x_10_out_3));
  or_x or_x_11 (.in_1(or_x_9_out_3), .in_2(in_1[14]), .out_3(or_x_11_out_3));
  or_x or_x_12 (.in_1(or_x_11_out_3), .in_2(in_1[15]), .out_3(out_2));
  or_x or_x_13 (.in_1(or_x_10_out_3), .in_2(in_1[7]), .out_3(or_x_13_out_3));
  or_x or_x_14 (.in_1(or_x_13_out_3), .in_2(in_1[8]), .out_3(or_x_14_out_3));
  or_x or_x_15 (.in_1(or_x_14_out_3), .in_2(in_1[9]), .out_3(or_x_15_out_3));
endmodule

module xor_x (
  input  in_1,
  input  in_2,
  output out_3
);

  wire and_x_1_out_3, and_x_2_out_3, not_x_1_out_2, not_x_2_out_2;

  not_x not_x_1 (.in_1(in_1), .out_2(not_x_1_out_2));
  and_x and_x_1 (.in_1(not_x_1_out_2), .in_2(in_2), .out_3(and_x_1_out_3));
  not_x not_x_2 (.in_1(in_2), .out_2(not_x_2_out_2));
  and_x and_x_2 (.in_1(not_x_2_out_2), .in_2(in_1), .out_3(and_x_2_out_3));
  or_x or_x_1 (.in_1(and_x_1_out_3), .in_2(and_x_2_out_3), .out_3(out_3));
endmodule

module mux_x (
  input  Select,
  input  D1,
  input  D0,
  output out_4
);

  wire and_x_1_out_3, and_x_2_out_3, not_x_1_out_2;

  not_x not_x_1 (.in_1(Select), .out_2(not_x_1_out_2));
  and_x and_x_1 (.in_1(not_x_1_out_2), .in_2(D0), .out_3(and_x_1_out_3));
  and_x and_x_2 (.in_1(D1), .in_2(Select), .out_3(and_x_2_out_3));
  or_x or_x_1 (.in_1(and_x_1_out_3), .in_2(and_x_2_out_3), .out_3(out_4));
endmodule

module dmux_x (
  input  select,
  input  in_2,
  output C1,
  output C0
);

  wire not_x_1_out_2;

  not_x not_x_1 (.in_1(select), .out_2(not_x_1_out_2));
  and_x and_x_1 (.in_1(select), .in_2(in_2), .out_3(C1));
  and_x and_x_2 (.in_1(not_x_1_out_2), .in_2(in_2), .out_3(C0));
endmodule

module mux4 (
  input  in_1,
  input  in_2,
  input  in_3,
  input  in_4,
  input  [1:0] in_5,
  output out_6
);

  wire mux_x_2_out_4, mux_x_3_out_4;

  mux_x mux_x_1 (.Select(in_5[1]), .D1(mux_x_2_out_4), .D0(mux_x_3_out_4), .out_4(out_6));
  mux_x mux_x_2 (.Select(in_5[0]), .D1(in_1), .D0(in_2), .out_4(mux_x_2_out_4));
  mux_x mux_x_3 (.Select(in_5[0]), .D1(in_3), .D0(in_4), .out_4(mux_x_3_out_4));
endmodule

module mux8 (
  input  in_1,
  input  in_2,
  input  in_3,
  input  in_4,
  input  in_5,
  input  in_6,
  input  in_7,
  input  in_8,
  input  [2:0] in_9,
  output out_10
);

  wire mux4_1_out_6, mux4_2_out_6;

  mux_x mux_x_1 (.Select(in_9[2]), .D1(mux4_1_out_6), .D0(mux4_2_out_6), .out_4(out_10));
  mux4 mux4_1 (.in_5(in_9[1:0]), .in_1(in_1), .in_2(in_2), .in_3(in_3), .in_4(in_4), .out_6(mux4_1_out_6));
  mux4 mux4_2 (.in_5(in_9[1:0]), .in_1(in_5), .in_2(in_6), .in_3(in_7), .in_4(in_8), .out_6(mux4_2_out_6));
endmodule

module dmux4 (
  input  [1:0] in_1,
  input  in_2,
  output out_3,
  output out_4,
  output out_5,
  output out_6
);

  wire dmux_x_1_c0, dmux_x_1_c1;

  dmux_x dmux_x_1 (.select(in_1[1]), .in_2(in_2), .C1(dmux_x_1_c1), .C0(dmux_x_1_c0));
  dmux_x dmux_x_2 (.select(in_1[0]), .in_2(dmux_x_1_c1), .C1(out_3), .C0(out_4));
  dmux_x dmux_x_3 (.select(in_1[0]), .in_2(dmux_x_1_c0), .C1(out_5), .C0(out_6));
endmodule

module dmux8 (
  input  [2:0] in_1,
  input  in_2,
  output out_3,
  output out_4,
  output out_5,
  output out_6,
  output out_7,
  output out_8,
  output out_9,
  output out_10
);

  wire dmux_x_1_c0, dmux_x_1_c1;

  dmux_x dmux_x_1 (.select(in_1[2]), .in_2(in_2), .C1(dmux_x_1_c1), .C0(dmux_x_1_c0));
  dmux4 dmux4_1 (.in_2(dmux_x_1_c1), .in_1(in_1[1:0]), .out_3(out_3), .out_4(out_4), .out_5(out_5), .out_6(out_6));
  dmux4 dmux4_2 (.in_2(dmux_x_1_c0), .in_1(in_1[1:0]), .out_3(out_7), .out_4(out_8), .out_5(out_9), .out_6(out_10));
endmodule

module not_x16 (
  input  [15:0] in_1,
  output [15:0] out_2
);

  not_x not_x_1 (.in_1(in_1[0]), .out_2(out_2[0]));
  not_x not_x_2 (.in_1(in_1[1]), .out_2(out_2[1]));
  not_x not_x_3 (.in_1(in_1[2]), .out_2(out_2[2]));
  not_x not_x_4 (.in_1(in_1[3]), .out_2(out_2[3]));
  not_x not_x_5 (.in_1(in_1[4]), .out_2(out_2[4]));
  not_x not_x_6 (.in_1(in_1[5]), .out_2(out_2[5]));
  not_x not_x_7 (.in_1(in_1[6]), .out_2(out_2[6]));
  not_x not_x_8 (.in_1(in_1[7]), .out_2(out_2[7]));
  not_x not_x_9 (.in_1(in_1[8]), .out_2(out_2[8]));
  not_x not_x_10 (.in_1(in_1[9]), .out_2(out_2[9]));
  not_x not_x_11 (.in_1(in_1[10]), .out_2(out_2[10]));
  not_x not_x_12 (.in_1(in_1[11]), .out_2(out_2[11]));
  not_x not_x_13 (.in_1(in_1[12]), .out_2(out_2[12]));
  not_x not_x_14 (.in_1(in_1[13]), .out_2(out_2[13]));
  not_x not_x_15 (.in_1(in_1[14]), .out_2(out_2[14]));
  not_x not_x_16 (.in_1(in_1[15]), .out_2(out_2[15]));
endmodule

module and_x16 (
  input  [15:0] in_1,
  input  [15:0] in_2,
  output [15:0] out_3
);

  and_x and_x_1 (.in_1(in_1[0]), .in_2(in_2[0]), .out_3(out_3[0]));
  and_x and_x_2 (.in_1(in_1[1]), .in_2(in_2[1]), .out_3(out_3[1]));
  and_x and_x_3 (.in_1(in_1[2]), .in_2(in_2[2]), .out_3(out_3[2]));
  and_x and_x_4 (.in_1(in_1[3]), .in_2(in_2[3]), .out_3(out_3[3]));
  and_x and_x_5 (.in_1(in_1[4]), .in_2(in_2[4]), .out_3(out_3[4]));
  and_x and_x_6 (.in_1(in_1[5]), .in_2(in_2[5]), .out_3(out_3[5]));
  and_x and_x_7 (.in_1(in_1[6]), .in_2(in_2[6]), .out_3(out_3[6]));
  and_x and_x_8 (.in_1(in_1[7]), .in_2(in_2[7]), .out_3(out_3[7]));
  and_x and_x_9 (.in_1(in_1[8]), .in_2(in_2[8]), .out_3(out_3[8]));
  and_x and_x_10 (.in_1(in_1[9]), .in_2(in_2[9]), .out_3(out_3[9]));
  and_x and_x_11 (.in_1(in_1[10]), .in_2(in_2[10]), .out_3(out_3[10]));
  and_x and_x_12 (.in_1(in_1[11]), .in_2(in_2[11]), .out_3(out_3[11]));
  and_x and_x_13 (.in_1(in_1[12]), .in_2(in_2[12]), .out_3(out_3[12]));
  and_x and_x_14 (.in_1(in_1[13]), .in_2(in_2[13]), .out_3(out_3[13]));
  and_x and_x_15 (.in_1(in_1[14]), .in_2(in_2[14]), .out_3(out_3[14]));
  and_x and_x_16 (.in_1(in_1[15]), .in_2(in_2[15]), .out_3(out_3[15]));
endmodule

module or_x16 (
  input  [15:0] in_1,
  input  [15:0] in_2,
  output [15:0] out_3
);

  or_x or_x_1 (.in_1(in_1[0]), .in_2(in_2[0]), .out_3(out_3[0]));
  or_x or_x_2 (.in_1(in_1[1]), .in_2(in_2[1]), .out_3(out_3[1]));
  or_x or_x_3 (.in_1(in_1[2]), .in_2(in_2[2]), .out_3(out_3[2]));
  or_x or_x_4 (.in_1(in_1[3]), .in_2(in_2[3]), .out_3(out_3[3]));
  or_x or_x_5 (.in_1(in_1[4]), .in_2(in_2[4]), .out_3(out_3[4]));
  or_x or_x_6 (.in_1(in_1[5]), .in_2(in_2[5]), .out_3(out_3[5]));
  or_x or_x_7 (.in_1(in_1[6]), .in_2(in_2[6]), .out_3(out_3[6]));
  or_x or_x_8 (.in_1(in_1[7]), .in_2(in_2[7]), .out_3(out_3[7]));
  or_x or_x_9 (.in_1(in_1[8]), .in_2(in_2[8]), .out_3(out_3[8]));
  or_x or_x_10 (.in_1(in_1[9]), .in_2(in_2[9]), .out_3(out_3[9]));
  or_x or_x_11 (.in_1(in_1[10]), .in_2(in_2[10]), .out_3(out_3[10]));
  or_x or_x_12 (.in_1(in_1[11]), .in_2(in_2[11]), .out_3(out_3[11]));
  or_x or_x_13 (.in_1(in_1[12]), .in_2(in_2[12]), .out_3(out_3[12]));
  or_x or_x_14 (.in_1(in_1[13]), .in_2(in_2[13]), .out_3(out_3[13]));
  or_x or_x_15 (.in_1(in_1[14]), .in_2(in_2[14]), .out_3(out_3[14]));
  or_x or_x_16 (.in_1(in_1[15]), .in_2(in_2[15]), .out_3(out_3[15]));
endmodule

module xor_x16 (
  input  [15:0] in_1,
  input  [15:0] in_2,
  output [15:0] out_3
);

  xor_x xor_x_1 (.in_1(in_1[0]), .in_2(in_2[0]), .out_3(out_3[0]));
  xor_x xor_x_2 (.in_1(in_1[1]), .in_2(in_2[1]), .out_3(out_3[1]));
  xor_x xor_x_3 (.in_1(in_1[2]), .in_2(in_2[2]), .out_3(out_3[2]));
  xor_x xor_x_4 (.in_1(in_1[3]), .in_2(in_2[3]), .out_3(out_3[3]));
  xor_x xor_x_5 (.in_1(in_1[4]), .in_2(in_2[4]), .out_3(out_3[4]));
  xor_x xor_x_6 (.in_1(in_1[5]), .in_2(in_2[5]), .out_3(out_3[5]));
  xor_x xor_x_7 (.in_1(in_1[6]), .in_2(in_2[6]), .out_3(out_3[6]));
  xor_x xor_x_8 (.in_1(in_1[7]), .in_2(in_2[7]), .out_3(out_3[7]));
  xor_x xor_x_9 (.in_1(in_1[8]), .in_2(in_2[8]), .out_3(out_3[8]));
  xor_x xor_x_10 (.in_1(in_1[9]), .in_2(in_2[9]), .out_3(out_3[9]));
  xor_x xor_x_11 (.in_1(in_1[10]), .in_2(in_2[10]), .out_3(out_3[10]));
  xor_x xor_x_12 (.in_1(in_1[11]), .in_2(in_2[11]), .out_3(out_3[11]));
  xor_x xor_x_13 (.in_1(in_1[12]), .in_2(in_2[12]), .out_3(out_3[12]));
  xor_x xor_x_14 (.in_1(in_1[13]), .in_2(in_2[13]), .out_3(out_3[13]));
  xor_x xor_x_15 (.in_1(in_1[14]), .in_2(in_2[14]), .out_3(out_3[14]));
  xor_x xor_x_16 (.in_1(in_1[15]), .in_2(in_2[15]), .out_3(out_3[15]));
endmodule

module mux_x16 (
  input  in_1,
  input  [15:0] in_2,
  input  [15:0] in_3,
  output [15:0] out_4
);

  mux_x mux_x_1 (.Select(in_1), .D1(in_2[15]), .D0(in_3[15]), .out_4(out_4[15]));
  mux_x mux_x_2 (.Select(in_1), .D1(in_2[14]), .D0(in_3[14]), .out_4(out_4[14]));
  mux_x mux_x_3 (.Select(in_1), .D1(in_2[13]), .D0(in_3[13]), .out_4(out_4[13]));
  mux_x mux_x_4 (.Select(in_1), .D1(in_2[12]), .D0(in_3[12]), .out_4(out_4[12]));
  mux_x mux_x_5 (.Select(in_1), .D1(in_2[11]), .D0(in_3[11]), .out_4(out_4[11]));
  mux_x mux_x_6 (.Select(in_1), .D1(in_2[10]), .D0(in_3[10]), .out_4(out_4[10]));
  mux_x mux_x_7 (.Select(in_1), .D1(in_2[9]), .D0(in_3[9]), .out_4(out_4[9]));
  mux_x mux_x_8 (.Select(in_1), .D1(in_2[8]), .D0(in_3[8]), .out_4(out_4[8]));
  mux_x mux_x_9 (.Select(in_1), .D1(in_2[7]), .D0(in_3[7]), .out_4(out_4[7]));
  mux_x mux_x_10 (.Select(in_1), .D1(in_2[6]), .D0(in_3[6]), .out_4(out_4[6]));
  mux_x mux_x_11 (.Select(in_1), .D1(in_2[5]), .D0(in_3[5]), .out_4(out_4[5]));
  mux_x mux_x_12 (.Select(in_1), .D1(in_2[4]), .D0(in_3[4]), .out_4(out_4[4]));
  mux_x mux_x_13 (.Select(in_1), .D1(in_2[3]), .D0(in_3[3]), .out_4(out_4[3]));
  mux_x mux_x_14 (.Select(in_1), .D1(in_2[2]), .D0(in_3[2]), .out_4(out_4[2]));
  mux_x mux_x_15 (.Select(in_1), .D1(in_2[1]), .D0(in_3[1]), .out_4(out_4[1]));
  mux_x mux_x_16 (.Select(in_1), .D1(in_2[0]), .D0(in_3[0]), .out_4(out_4[0]));
endmodule

module mux4_x16 (
  input  [15:0] in_1,
  input  [15:0] in_2,
  input  [15:0] in_3,
  input  [15:0] in_4,
  input  [1:0] in_5,
  output [15:0] out_6
);

  wire [15:0] mux_x16_2_out_4, mux_x16_3_out_4;

  mux_x16 mux_x16_1 (.in_1(in_5[1]), .in_2(mux_x16_2_out_4), .in_3(mux_x16_3_out_4), .out_4(out_6));
  mux_x16 mux_x16_2 (.in_1(in_5[0]), .in_2(in_1), .in_3(in_2), .out_4(mux_x16_2_out_4));
  mux_x16 mux_x16_3 (.in_1(in_5[0]), .in_2(in_3), .in_3(in_4), .out_4(mux_x16_3_out_4));
endmodule

module mux8_x16 (
  input  [15:0] in_1,
  input  [15:0] in_2,
  input  [15:0] in_3,
  input  [15:0] in_4,
  input  [15:0] in_5,
  input  [15:0] in_6,
  input  [15:0] in_7,
  input  [15:0] in_8,
  input  [2:0] in_9,
  output [15:0] out_10
);

  wire [15:0] mux4_x16_1_out_6, mux4_x16_2_out_6;

  mux_x16 mux_x16_1 (.in_1(in_9[2]), .in_2(mux4_x16_1_out_6), .in_3(mux4_x16_2_out_6), .out_4(out_10));
  mux4_x16 mux4_x16_1 (.in_5(in_9[1:0]), .in_1(in_1), .in_2(in_2), .in_3(in_3), .in_4(in_4), .out_6(mux4_x16_1_out_6));
  mux4_x16 mux4_x16_2 (.in_5(in_9[1:0]), .in_1(in_5), .in_2(in_6), .in_3(in_7), .in_4(in_8), .out_6(mux4_x16_2_out_6));
endmodule

module dmux_x16 (
  input  in_1,
  input  [15:0] in_2,
  output [15:0] out_3,
  output [15:0] out_4
);

  dmux_x dmux_x_1 (.select(in_1), .in_2(in_2[14]), .C1(out_3[14]), .C0(out_4[14]));
  dmux_x dmux_x_2 (.select(in_1), .in_2(in_2[15]), .C1(out_3[15]), .C0(out_4[15]));
  dmux_x dmux_x_3 (.select(in_1), .in_2(in_2[13]), .C1(out_3[13]), .C0(out_4[13]));
  dmux_x dmux_x_4 (.select(in_1), .in_2(in_2[11]), .C1(out_3[11]), .C0(out_4[11]));
  dmux_x dmux_x_5 (.select(in_1), .in_2(in_2[12]), .C1(out_3[12]), .C0(out_4[12]));
  dmux_x dmux_x_6 (.select(in_1), .in_2(in_2[10]), .C1(out_3[10]), .C0(out_4[10]));
  dmux_x dmux_x_7 (.select(in_1), .in_2(in_2[8]), .C1(out_3[8]), .C0(out_4[8]));
  dmux_x dmux_x_8 (.select(in_1), .in_2(in_2[9]), .C1(out_3[9]), .C0(out_4[9]));
  dmux_x dmux_x_9 (.select(in_1), .in_2(in_2[6]), .C1(out_3[6]), .C0(out_4[6]));
  dmux_x dmux_x_10 (.select(in_1), .in_2(in_2[7]), .C1(out_3[7]), .C0(out_4[7]));
  dmux_x dmux_x_11 (.select(in_1), .in_2(in_2[5]), .C1(out_3[5]), .C0(out_4[5]));
  dmux_x dmux_x_12 (.select(in_1), .in_2(in_2[3]), .C1(out_3[3]), .C0(out_4[3]));
  dmux_x dmux_x_13 (.select(in_1), .in_2(in_2[4]), .C1(out_3[4]), .C0(out_4[4]));
  dmux_x dmux_x_14 (.select(in_1), .in_2(in_2[2]), .C1(out_3[2]), .C0(out_4[2]));
  dmux_x dmux_x_15 (.select(in_1), .in_2(in_2[0]), .C1(out_3[0]), .C0(out_4[0]));
  dmux_x dmux_x_16 (.select(in_1), .in_2(in_2[1]), .C1(out_3[1]), .C0(out_4[1]));

  // Other names for the same wires on the sheet: I0 = in_2[0]; I1 = in_2[1]; I2 = in_2[2]; I3 = in_2[3]; I4 = in_2[4];
  //   I5 = in_2[5]; I6 = in_2[6]; I7 = in_2[7]; I8 = in_2[8]; I9 = in_2[9]; I10 = in_2[10]; I11 = in_2[11];
  //   I12 = in_2[12]; I13 = in_2[13]; I14 = in_2[14]; I15 = in_2[15]; D1_0 = out_3[0]; D1_1 = out_3[1];
  //   D1_2 = out_3[2]; D1_3 = out_3[3]; D1_4 = out_3[4]; D1_5 = out_3[5]; D1_6 = out_3[6]; D1_7 = out_3[7];
  //   D1_8 = out_3[8]; D1_9 = out_3[9]; D1_10 = out_3[10]; D1_11 = out_3[11]; D1_12 = out_3[12]; D1_13 = out_3[13];
  //   D1_14 = out_3[14]; D1_15 = out_3[15]; D0_0 = out_4[0]; D0_1 = out_4[1]; D0_2 = out_4[2]; D0_3 = out_4[3];
  //   D0_4 = out_4[4]; D0_5 = out_4[5]; D0_6 = out_4[6]; D0_7 = out_4[7]; D0_8 = out_4[8]; D0_9 = out_4[9];
  //   D0_10 = out_4[10]; D0_11 = out_4[11]; D0_12 = out_4[12]; D0_13 = out_4[13]; D0_14 = out_4[14];
  //   D0_15 = out_4[15]
endmodule

module dmux4_x16 (
  input  [1:0] in_1,
  input  [15:0] in_2,
  output [15:0] out_3,
  output [15:0] out_4,
  output [15:0] out_5,
  output [15:0] out_6
);

  wire [15:0] dmux_x16_1_out_3, dmux_x16_1_out_4;

  dmux_x16 dmux_x16_1 (.in_1(in_1[1]), .in_2(in_2), .out_3(dmux_x16_1_out_3), .out_4(dmux_x16_1_out_4));
  dmux_x16 dmux_x16_2 (.in_1(in_1[0]), .in_2(dmux_x16_1_out_3), .out_3(out_3), .out_4(out_4));
  dmux_x16 dmux_x16_3 (.in_1(in_1[0]), .in_2(dmux_x16_1_out_4), .out_3(out_5), .out_4(out_6));
endmodule

module dmux8_x16 (
  input  [2:0] in_1,
  input  [15:0] in_2,
  output [15:0] out_3,
  output [15:0] out_4,
  output [15:0] out_5,
  output [15:0] out_6,
  output [15:0] out_7,
  output [15:0] out_8,
  output [15:0] out_9,
  output [15:0] out_10
);

  wire [15:0] dmux_x16_1_out_3, dmux_x16_1_out_4;

  dmux_x16 dmux_x16_1 (.in_1(in_1[2]), .in_2(in_2), .out_3(dmux_x16_1_out_3), .out_4(dmux_x16_1_out_4));
  dmux4_x16 dmux4_x16_1 (
    .in_2(dmux_x16_1_out_3), .in_1(in_1[1:0]), .out_3(out_3), .out_4(out_4), .out_5(out_5), .out_6(out_6));
  dmux4_x16 dmux4_x16_2 (
    .in_2(dmux_x16_1_out_4), .in_1(in_1[1:0]), .out_3(out_7), .out_4(out_8), .out_5(out_9), .out_6(out_10));
endmodule

// VHDL entity nand_vhd_x, as the project stores it:
library IEEE;
use IEEE.std_logic_1164.all;

entity nand_vhd_x is
    Port (
        A: in   STD_LOGIC;
        B: in   STD_LOGIC;
        Y: out  STD_LOGIC
    );
end nand_vhd_x;

architecture default of nand_vhd_x is
begin
    Y <= not (A and B);
end default;

// VHDL entity not_vhd_x, as the project stores it:
library IEEE;
use IEEE.std_logic_1164.all;

entity not_vhd_x is
    Port (
        I: in   STD_LOGIC;
        O: out  STD_LOGIC
    );
end not_vhd_x;

architecture default of not_vhd_x is
    component nand_vhd_x
        Port (
            A: in   STD_LOGIC;
            B: in   STD_LOGIC;
            Y: out  STD_LOGIC
        );
    end component;
begin
    connect: nand_vhd_x port map (I, I, O);
end default;

// VHDL entity and_vhd_x, as the project stores it:
library IEEE;
use IEEE.std_logic_1164.all;

entity and_vhd_x is
    Port (
        A: in   STD_LOGIC;
        B: in   STD_LOGIC;
        Y: out  STD_LOGIC
    );
end and_vhd_x;

architecture default of and_vhd_x is
    component nand_vhd_x
        Port (
            A: in   STD_LOGIC;
            B: in   STD_LOGIC;
            Y: out  STD_LOGIC
        );
    end component;
    component not_vhd_x
        Port (
            I: in   STD_LOGIC;
            O: out  STD_LOGIC
        );
    end component;

    signal NAND_O: STD_LOGIC;
    
begin
    connection1: nand_vhd_x port map (A, B, NAND_O);
    connection2: not_vhd_x port map (NAND_O, Y);
end default;

// VHDL entity or_vhd_x, as the project stores it:
library IEEE;
use IEEE.std_logic_1164.all;

entity or_vhd_x is
    Port (
        A: in   STD_LOGIC;
        B: in   STD_LOGIC;
        O: out  STD_LOGIC
    );
end or_vhd_x;

architecture default of or_vhd_x is
    component nand_vhd_x
        Port (
            A: in   STD_LOGIC;
            B: in   STD_LOGIC;
            Y: out  STD_LOGIC
        );
    end component;
    component not_vhd_x
        Port (
            I: in   STD_LOGIC;
            O: out  STD_LOGIC
        );
    end component;

    signal NOT_A: STD_LOGIC;
    signal NOT_B: STD_LOGIC;

begin
    reverse_a   : not_vhd_x port map (A, NOT_A);
    reverse_b   : not_vhd_x port map (B, NOT_B);
    nand_ab     : nand_vhd_x port map (NOT_A, NOT_B, O);
end default;

// VHDL entity not_zero_vhd_x16, as the project stores it:
library IEEE;
use IEEE.std_logic_1164.all;

entity not_zero_vhd_x16 is
    Port (
        I: in   STD_LOGIC_VECTOR (15 downto 0);
        O: out  STD_LOGIC
    );
end not_zero_vhd_x16;

architecture default of not_zero_vhd_x16 is
    component or_vhd_x
        Port (
            A: in   STD_LOGIC;
            B: in   STD_LOGIC;
            O: out  STD_LOGIC
        );
    end component;

    signal OR1: STD_LOGIC;
    signal OR2: STD_LOGIC;
    signal OR3: STD_LOGIC;
    signal OR4: STD_LOGIC;
    signal OR5: STD_LOGIC;
    signal OR6: STD_LOGIC;
    signal OR7: STD_LOGIC;
    signal OR8: STD_LOGIC;
    signal OR9: STD_LOGIC;
    signal OR10: STD_LOGIC;
    signal OR11: STD_LOGIC;
    signal OR12: STD_LOGIC;
    signal OR13: STD_LOGIC;
    signal OR14: STD_LOGIC;
    signal OR15: STD_LOGIC;

begin
    or_1:   or_vhd_x port map (I(0), I(1), OR1);
    or_2:   or_vhd_x port map (OR1, I(2), OR2);
    or_3:   or_vhd_x port map (OR2, I(3), OR3);
    or_4:   or_vhd_x port map (OR3, I(4), OR4);
    or_5:   or_vhd_x port map (OR4, I(5), OR5);
    or_6:   or_vhd_x port map (OR5, I(6), OR6);
    or_7:   or_vhd_x port map (OR6, I(7), OR7);
    or_8:   or_vhd_x port map (OR7, I(8), OR8);
    or_9:   or_vhd_x port map (OR8, I(9), OR9);
    or_10:  or_vhd_x port map (OR9, I(10), OR10);
    or_11:  or_vhd_x port map (OR10, I(11), OR11);
    or_12:  or_vhd_x port map (OR11, I(12), OR12);
    or_13:  or_vhd_x port map (OR12, I(13), OR13);
    or_14:  or_vhd_x port map (OR13, I(14), OR14);
    or_15:  or_vhd_x port map (OR14, I(15), OR15);
    O <= OR15;
end default;

// VHDL entity xor_vhd_x, as the project stores it:
library IEEE;
use IEEE.std_logic_1164.all;

entity xor_vhd_x is
    Port (
        A: in   STD_LOGIC;
        B: in   STD_LOGIC;
        O: out  STD_LOGIC
    );
end xor_vhd_x;

architecture default of xor_vhd_x is
    component not_vhd_x
        Port (
            I: in   STD_LOGIC;
            O: out  STD_LOGIC
        );
    end component;
    component and_vhd_x
        Port (
            A: in   STD_LOGIC;
            B: in   STD_LOGIC;
            Y: out  STD_LOGIC
        );
    end component;
    component or_vhd_x
        Port (
            A: in   STD_LOGIC;
            B: in   STD_LOGIC;
            O: out  STD_LOGIC
        );
    end component;

    signal NOT_A: STD_LOGIC;
    signal NOT_B: STD_LOGIC;
    signal NOT_A_AND_B: STD_LOGIC;
    signal NOT_B_AND_A: STD_LOGIC;

begin
    reverse_a   : not_vhd_x port map (A, NOT_A);
    reverse_b   : not_vhd_x port map (B, NOT_B);
    and1        : and_vhd_x port map (NOT_A, B, NOT_A_AND_B);
    and2        : and_vhd_x port map (A, NOT_B, NOT_B_AND_A);
    last        : or_vhd_x  port map (NOT_A_AND_B, NOT_B_AND_A, O);
end default;

// VHDL entity mux_vhd_x, as the project stores it:
library IEEE;
use IEEE.std_logic_1164.all;

entity mux_vhd_x is
    Port (
        S   : in    STD_LOGIC;
        D1  : in    STD_LOGIC;
        D0  : in    STD_LOGIC;
        O   : out   STD_LOGIC
    );
end mux_vhd_x;

architecture default of mux_vhd_x is
    component not_vhd_x
        Port (
            I: in   STD_LOGIC;
            O: out  STD_LOGIC
        );
    end component;
    component and_vhd_x
        Port (
            A: in   STD_LOGIC;
            B: in   STD_LOGIC;
            Y: out  STD_LOGIC
        );
    end component;
    component or_vhd_x
        Port (
            A: in   STD_LOGIC;
            B: in   STD_LOGIC;
            O: out  STD_LOGIC
        );
    end component;

    signal NOT_SELECT        : STD_LOGIC;
    signal NOT_SELECT_AND_D0 : STD_LOGIC;
    signal SELECT_AND_D1     : STD_LOGIC;

begin
    reverse_s : not_vhd_x port map (S, NOT_SELECT);
    data0     : and_vhd_x port map (NOT_SELECT, D0, NOT_SELECT_AND_D0);
    data1     : and_vhd_x port map (S, D1, SELECT_AND_D1);
    last      : or_vhd_x  port map (NOT_SELECT_AND_D0, SELECT_AND_D1, O);
end default;

// VHDL entity dmux_vhd_x, as the project stores it:
library IEEE;
use IEEE.std_logic_1164.all;

entity dmux_vhd_x is
    Port (
        S: in   STD_LOGIC;
        D: in   STD_LOGIC;
        O1: out  STD_LOGIC;
        O0: out  STD_LOGIC
    );
end dmux_vhd_x;

architecture default of dmux_vhd_x is
    component not_vhd_x
        Port (
            I: in   STD_LOGIC;
            O: out  STD_LOGIC
        );
    end component;
    component and_vhd_x
        Port (
            A: in   STD_LOGIC;
            B: in   STD_LOGIC;
            Y: out  STD_LOGIC
        );
    end component;

    signal NOT_SELECT: STD_LOGIC;

begin
    reverse_s : not_vhd_x port map (S, NOT_SELECT);
    low_bit   : and_vhd_x port map (NOT_SELECT, D, O0);
    high_bit  : and_vhd_x port map (S, D, O1);
end default;

// VHDL entity mux4_vhd_x, as the project stores it:
library IEEE;
use IEEE.std_logic_1164.all;

entity mux4_vhd_x is
    Port (
        S   : in    STD_LOGIC_VECTOR (1 downto 0);
        I3  : in    STD_LOGIC;
        I2  : in    STD_LOGIC;
        I1  : in    STD_LOGIC;
        I0  : in    STD_LOGIC;
        O   : out   STD_LOGIC
    );
end mux4_vhd_x;

architecture default of mux4_vhd_x is
    component mux_vhd_x is
        Port (
            S   : in    STD_LOGIC;
            D1  : in    STD_LOGIC;
            D0  : in    STD_LOGIC;
            O   : out   STD_LOGIC
        );
    end component;

    signal H: STD_LOGIC;
    signal L: STD_LOGIC;

begin
    get_high : mux_vhd_x port map (S(0), I3, I2, H);
    get_low  : mux_vhd_x port map (S(0), I1, I0, L);
    last     : mux_vhd_x port map (S(1), H, L, O);
end default;

// VHDL entity mux8_vhd_x, as the project stores it:
library IEEE;
use IEEE.std_logic_1164.all;

entity mux8_vhd_x is
    Port (
        S   : in    STD_LOGIC_VECTOR (2 downto 0);
        I7  : in    STD_LOGIC;
        I6  : in    STD_LOGIC;
        I5  : in    STD_LOGIC;
        I4  : in    STD_LOGIC;
        I3  : in    STD_LOGIC;
        I2  : in    STD_LOGIC;
        I1  : in    STD_LOGIC;
        I0  : in    STD_LOGIC;
        O   : out   STD_LOGIC
    );
end mux8_vhd_x;

architecture default of mux8_vhd_x is
    component mux_vhd_x is
        Port (
            S   : in    STD_LOGIC;
            D1  : in    STD_LOGIC;
            D0  : in    STD_LOGIC;
            O   : out   STD_LOGIC
        );
    end component;
    component mux4_vhd_x is
        Port (
            S   : in    STD_LOGIC_VECTOR (1 downto 0);
            I3  : in    STD_LOGIC;
            I2  : in    STD_LOGIC;
            I1  : in    STD_LOGIC;
            I0  : in    STD_LOGIC;
            O   : out   STD_LOGIC
        );
    end component;

    signal H: STD_LOGIC;
    signal L: STD_LOGIC;

begin
    get_high: mux4_vhd_x port map (S(1 downto 0), I7, I6, I5, I4, H);
    get_low : mux4_vhd_x port map (S(1 downto 0), I3, I2, I1, I0, L);
    last    : mux_vhd_x  port map (S(2), H, L, O);
end default;

// VHDL entity dmux4_vhd_x, as the project stores it:
library IEEE;
use IEEE.std_logic_1164.all;

entity dmux4_vhd_x is
    Port (
        S   : in    STD_LOGIC_VECTOR (1 downto 0);
        I   : in    STD_LOGIC;
        O3  : out   STD_LOGIC;
        O2  : out   STD_LOGIC;
        O1  : out   STD_LOGIC;
        O0  : out   STD_LOGIC
    );
end dmux4_vhd_x;

architecture default of dmux4_vhd_x is
    component dmux_vhd_x is
        Port (
            S: in   STD_LOGIC;
            D: in   STD_LOGIC;
            O1: out  STD_LOGIC;
            O0: out  STD_LOGIC
        );
    end component;

    signal H: STD_LOGIC;
    signal L: STD_LOGIC;

begin
    locate      : dmux_vhd_x port map (S(1), I, H, L);
    output_high : dmux_vhd_x port map (S(0), H, O3, O2);
    output_low  : dmux_vhd_x port map (S(0), L, O1, O0);
end default;

// VHDL entity dmux8_vhd_x, as the project stores it:
library IEEE;
use IEEE.std_logic_1164.all;

entity dmux8_vhd_x is
    Port (
        S   : in  STD_LOGIC_VECTOR (2 downto 0);
        I   : in  STD_LOGIC;
        O7  : out STD_LOGIC;
        O6  : out STD_LOGIC;
        O5  : out STD_LOGIC;
        O4  : out STD_LOGIC;
        O3  : out STD_LOGIC;
        O2  : out STD_LOGIC;
        O1  : out STD_LOGIC;
        O0  : out STD_LOGIC
    );
end dmux8_vhd_x;

architecture default of dmux8_vhd_x is
    component dmux_vhd_x is
        Port (
            S: in   STD_LOGIC;
            D: in   STD_LOGIC;
            O1: out  STD_LOGIC;
            O0: out  STD_LOGIC
        );
    end component;
    component dmux4_vhd_x is
        Port (
            S   : in    STD_LOGIC_VECTOR (1 downto 0);
            I   : in    STD_LOGIC;
            O3  : out   STD_LOGIC;
            O2  : out   STD_LOGIC;
            O1  : out   STD_LOGIC;
            O0  : out   STD_LOGIC
        );
    end component;

    signal H: STD_LOGIC;
    signal L: STD_LOGIC;
    
begin
    locate      : dmux_vhd_x port map (S(2), I, H, L);
    output_high : dmux4_vhd_x port map (S(1 downto 0), H, O7, O6, O5, O4);
    output_low  : dmux4_vhd_x port map (S(1 downto 0), L, O3, O2, O1, O0);
end architecture default;
